# Fritzing sketch ESP (saved by Fritzing 0.9.3b)
breadboards: 1

parts:
  DHT1 = DHT22 Humidity and Temperature Sensor
  U1 = NodeMCU V1.0

nets:
  VDD: DHT1.VDD, U1.Vin
  N1: DHT1.DATA, U1.D2
  GND: DHT1.GND, U1.GND

custom parts:
  NodeMCU V1.0: ESP8266 based NodeMCU
