# Fritzing sketch sgh-controller (saved by Fritzing 0.9.3b)
breadboards: 1

parts:
  Componente1 = Arduino Uno (Rev3)
  LED1 = LED - 5mm [color="Red (633nm)" package="5 mm [THT]"]
  LED2 = LED - 5mm [color="Green (555nm)" package="5 mm [THT]"]
  LED3 = LED - 5mm [color="Green (555nm)" package="5 mm [THT]"]
  R1 = Resistor [tolerance=±5% resistance=220 package=THT]
  R2 = Resistor [tolerance=±5% resistance=220 package=THT]
  R3 = Resistor [tolerance=±5% resistance=220 package=THT]
  Componente2 = Bluetooth HC-05 Macho
  J1 = Basic Servo
  hc-sr1 = hc-sr04

nets:
  N1: Componente1.D12/MISO, R3.Pin_1
  N2: Componente1.D13/SCK, R1.Pin_1
  GND: Componente1.GND, LED1.cathode, LED2.cathode, LED3.cathode, Componente2.GND, J1.gnd, hc-sr1.GND
  N3: Componente1.D2, Componente2.TXD
  N4: Componente1.D4, hc-sr1.Trig
  N5: Componente1.D5_PWM, R2.Pin_1
  N6: Componente1.D6_PWM, Componente2.RXD
  N7: Componente1.D7, hc-sr1.Echo
  VCC: Componente1.5V, Componente2.VCC, J1.vcc, hc-sr1.VCC
  N8: LED1.anode, R3.Pin_0
  N9: LED2.anode, R1.Pin_0
  N10: LED3.anode, R2.Pin_0
